# Fritzing sketch Circuit_Diagram (saved by Fritzing 0.9.3b)

parts:
  U1 = ESP8266 NodeMCU LoLin module
  S1 = H-Bridge with L298N
  M1 = DC Motor
  M2 = DC Motor
  M3 = DC Motor
  M4 = DC Motor
  VCC1 = 4 x AAA Battery Mount

nets:
  N1: U1.D0, S1.ENA
  N2: U1.D1, S1.IN1
  N3: U1.D2, S1.IN2
  N4: U1.D3, S1.IN3
  N5: U1.D4, S1.IN4
  GND: U1.GND, S1.GND, VCC1.-
  N6: U1.D5, S1.ENB
  VIN: U1.Vin, S1.5V
  N7: S1.12V, VCC1.+
  N8: S1.M1-01, M1.pin_2, M2.pin_2
  N9: S1.M1-02, M1.pin_1, M2.pin_1
  N10: S1.M2-01, M3.pin_2, M4.pin_2
  N11: S1.M2-02, M3.pin_1, M4.pin_1

custom parts:
  ESP8266 NodeMCU LoLin module: ESP8266 based NodeMCU
  H-Bridge with L298N: h-bridge
